# Fritzing sketch smartbin (saved by Fritzing 0.9.10b)
circuit board: 8.46667cm x 5.64444cm
breadboards: 1

parts:
  HC-SR04_Sensor_1 = HC-SR04 Ultrasonic Distance Sensor
  Part1 = Arduino Nano (Rev3.0)
  J1 = Basic Servo
  C1 = Capacitor Polarized [package=panasonic_e]

nets:
  VCC: HC-SR04_Sensor_1.VCC, Part1.5V, J1.vcc, C1.+
  N1: HC-SR04_Sensor_1.TRIG, Part1.D3
  N2: HC-SR04_Sensor_1.ECHO, Part1.D2
  GND: HC-SR04_Sensor_1.GND, Part1.GND, J1.gnd, C1.-
  N3: Part1.D5, J1.pulse
